// Logisim project Temp.circ as structural Verilog: 1 circuit, main circuit Temp
module Temp (
  input  [3:0] in_1,
  input  CLK,
  input  Clear,
  output out_4
);

  wire [3:0] counter_1_q;

  Counter #(.width(4), .max('hf)) counter_1 (.Q(counter_1_q), .clk(CLK), .clr(Clear));  // open: load, D, count, carry
  Comparator #(.width(4)) comparator_1 (.a(in_1), .b(counter_1_q), .eq(out_4));  // open: gt, lt

  // Notes on the sheet:
  //   TEMP
endmodule
